# Fritzing sketch lcd (saved by Fritzing 0.9.3b)
breadboards: 1

parts:
  Raspberry_Pi_B_rev1 = Raspberry Pi B rev1
  Bolymin_BC2004A = LCD screen
  PSU = DC Power [voltage=5V]
  R3 = Trimmer Potentiometer [maximum_resistance=10kΩ package=THT]
  R4 = Resistor [tolerance=±5% resistance=100 package="0805 [SMD]"]
  R5 = Resistor [tolerance=±5% resistance=100 package="0805 [SMD]"]
  R6 = Slide Potentiometer [maximum_resistance=100Ω]

nets:
  5V: Raspberry_Pi_B_rev1.5V, Bolymin_BC2004A.VDD, R6.leg1
  GND: Raspberry_Pi_B_rev1.GND, Bolymin_BC2004A.VSS, Bolymin_BC2004A.R/W, R6.wiper
  N1: Raspberry_Pi_B_rev1.GPIO_23, Bolymin_BC2004A.DB6
  N2: Raspberry_Pi_B_rev1.GPIO_18, Bolymin_BC2004A.DB7
  N3: Raspberry_Pi_B_rev1.GPIO_24, Bolymin_BC2004A.DB5
  N4: Raspberry_Pi_B_rev1.GPIO_25, Bolymin_BC2004A.DB4
  N5: Raspberry_Pi_B_rev1.GPIO_8, Bolymin_BC2004A.E
  N6: Raspberry_Pi_B_rev1.GPIO_7, Bolymin_BC2004A.RS
  N7: Bolymin_BC2004A.V0, R6.leg2
  N8: Bolymin_BC2004A.LED+, R4.Pin_0, R5.Pin_0
  N9: Bolymin_BC2004A.LED-, PSU.V-, R3.leg2
  N10: PSU.V+, R3.leg1
  N11: R3.wiper, R5.Pin_1
