# Fritzing sketch rotary (saved by Fritzing 0.9.3b)
breadboards: 1

parts:
  Drehimpulsgeber = Rotary Encoder [package=THT]
  Raspberry_Pi_B_rev1 = Raspberry Pi B rev1
  Drehimpulsgeber-Schalter = SWITCH-MOMENTARY-2 [package=tactile_switch_smd-2]

nets:
  N1: Drehimpulsgeber.EncoderPinA, Raspberry_Pi_B_rev1.GPIO_10
  N2: Drehimpulsgeber.EncoderPinC, Raspberry_Pi_B_rev1.GND, Drehimpulsgeber-Schalter.1
  N3: Drehimpulsgeber.EncoderPinB, Raspberry_Pi_B_rev1.GPIO_9
  N4: Raspberry_Pi_B_rev1.GPIO_11, Drehimpulsgeber-Schalter.2
