# Fritzing sketch led (saved by Fritzing 0.9.3b)
breadboards: 1

parts:
  R = Resistor [tolerance=±5% resistance=100 package=THT]
  LED_RED = smd LED [color="Red (633nm)" package="0805 [SMD]"]
  Raspberry_Pi = Raspberry Pi B rev1

nets:
  N1: R.Pin_0, Raspberry_Pi.GPIO_24
  N2: R.Pin_1, LED_RED.anode
  N3: LED_RED.cathode, Raspberry_Pi.GND
