# Fritzing sketch transistor_led (saved by Fritzing 0.9.2b)
breadboards: 1

parts:
  BC547_RED = NPN-Transistor [package="SOT-23 [SMD]"]
  BC547_GREEN = NPN-Transistor [package="SOT-23 [SMD]"]
  BC547_BLUE = NPN-Transistor [package="SOT-23 [SMD]"]
  R_BLUE = Resistor [tolerance=±5% resistance=10k package="2010 [SMD]"]
  R_GREEN = Resistor [tolerance=±5% resistance=10k package="2010 [SMD]"]
  RGB_LED_2 = RGB LED - (4 legs) [package="5 mm [THT]"]
  R4 = Resistor [tolerance=±5% resistance=220 package="2010 [SMD]"]
  R5 = Resistor [tolerance=±5% resistance=100 package="2010 [SMD]"]
  R6 = Resistor [tolerance=±5% resistance=100 package="2010 [SMD]"]
  RGB_LED_3 = RGB LED - (4 legs) [package="5 mm [THT]"]
  R7 = Resistor [tolerance=±5% resistance=100 package="2010 [SMD]"]
  R8 = Resistor [tolerance=±5% resistance=220 package="2010 [SMD]"]
  R9 = Resistor [tolerance=±5% resistance=100 package="2010 [SMD]"]
  R10 = Resistor [tolerance=±5% resistance=220 package="2010 [SMD]"]
  R11 = Resistor [tolerance=±5% resistance=100 package="2010 [SMD]"]
  R_RED = Resistor [tolerance=±5% resistance=10k package="2010 [SMD]"]
  Raspberry_Pi = Raspberry Pi B rev1
  PSU = DC Power [voltage=5V frequency=60]
  R12 = Resistor [tolerance=±5% resistance=100 package="1206 [SMD]"]
  RGB_LED_1 = RGB LED - (4 legs) [package="5 mm [THT]"]

nets:
  N1: BC547_RED.2, BC547_GREEN.2, BC547_BLUE.2, Raspberry_Pi.GND, PSU.V-
  N2: BC547_RED.0, R_RED.Pin_1
  N3: BC547_RED.1, R4.Pin_1, R8.Pin_1, R10.Pin_1
  N4: BC547_GREEN.0, R_GREEN.Pin_1
  N5: BC547_GREEN.1, R5.Pin_1, R9.Pin_1, R11.Pin_1
  N6: BC547_BLUE.0, R_BLUE.Pin_1
  N7: BC547_BLUE.1, R6.Pin_1, R7.Pin_1, R12.Pin_1
  N8: R_BLUE.Pin_0, Raspberry_Pi.GIPO_0
  N9: R_GREEN.Pin_0, Raspberry_Pi.GIPO_1
  N10: RGB_LED_2.red_cathode, R4.Pin_0
  N11: RGB_LED_2.common_anode, RGB_LED_3.common_anode, PSU.V+, RGB_LED_1.common_anode
  N12: RGB_LED_2.green_cathode, R5.Pin_0
  N13: RGB_LED_2.blue_cathode, R6.Pin_0
  N14: RGB_LED_3.red_cathode, R8.Pin_0
  N15: RGB_LED_3.green_cathode, R9.Pin_0
  N16: RGB_LED_3.blue_cathode, R7.Pin_0
  N17: R10.Pin_0, RGB_LED_1.red_cathode
  N18: R11.Pin_0, RGB_LED_1.green_cathode
  N19: R_RED.Pin_0, Raspberry_Pi.GPIO_23
  N20: R12.Pin_0, RGB_LED_1.blue_cathode
